# Fritzing sketch smart-door-lock-circuit-diagram (saved by Fritzing 1.0.5)
breadboards: 1

parts:
  Part1 = HC-05 [part_number=HC-05 package="breakout board"]
  U1 = LuaNode32 / ESP32 [part_number=ESP32S-PIN30]
  SG1 = Buzzer 12mm [part_number=COM-07950 package=buzzer-12mm-ns]
  DHT11_1 = DHT11 module
  Part2 = 4x4 Keypad [part_number=101207]
  Part3 = RFID-RC522 [part_number=101218]
  SERVO1 = Tower Pro SG90 servo [part_number=101246]
  LCD2004-I2C1 = LCD2004-I2C

nets:
  VCC: Part1.VCC, U1.Vin, DHT11_1.VCC, SERVO1.+5V, LCD2004-I2C1.VCC
  GND: Part1.GND, U1.GND, SG1.2, DHT11_1.GND, Part3.GND, SERVO1.GND, LCD2004-I2C1.GND
  N1: Part1.TXD, U1.RX2
  N2: Part1.RXD, U1.TX2
  N3: U1.D32, Part2.8
  N4: U1.D33, Part2.7
  N5: U1.D25, Part2.6
  N6: U1.D26, Part2.5
  N7: U1.D27, Part2.4
  N8: U1.D14, Part2.3
  N9: U1.D12, Part2.2
  N10: U1.D13, Part2.1
  3V3: U1.3V3, Part3.RST, Part3.3.3V
  N11: U1.D15, LCD2004-I2C1.SCL
  N12: U1.D2, LCD2004-I2C1.SDA
  N13: U1.D4, DHT11_1.DATA
  N14: U1.D5, SG1.1
  N15: U1.D18, SERVO1.Signal
  N16: U1.D19, Part3.MISO
  N17: U1.D21, Part3.MOSI
  N18: U1.D22, Part3.SCK
  N19: U1.D23, Part3.SDA

custom parts:
  HC-05: A commonly available HC-05 Bluetooth breakout board.
  LuaNode32 / ESP32: New Image for LuaNode32 DOIT ESP32 DEVKIT V1. Base parts from LuaNode32 / ESP32 ESP32 based LuaNode32 by G.Noorlander DOIT Esp32 DevKit v1 (30 pins long, 11 pins width) by Werner Rothschopf (modified by vanepp Dec 2018)
  Buzzer 12mm: Buzzer 12mm Spark Fun Electronics SKU : Comp-Buzzer Through hole This is a small 12mm round speaker that operates around the audible 2kHz range. You can use these speakers to create simple music or user interfaces. This is not a true piezoelectric speaker but behaves similarly. Instead of a piezoelectric crystal that vibrates with an electric current, this tiny speaker uses an electromagnet to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
  DHT11 module: https://cdn-learn.adafruit.com/downloads/pdf/dht.pdf DHT11 black pcb module reference by:https://github.com/adafruit/Fritzing-Library/blob/master/parts/DHT11%20Humitidy%20and%20Temperature%20Sensor.fzpz
  4x4 Keypad: Matrix membrane keypad 4x4
  Tower Pro SG90 servo: Original file by John De Cristofaro http://www.adafruit.com/products/1449 Adafruit Feedback Servo (Small) Edited by: e-radionica.com 28/9/2015
  LCD2004-I2C: A standard character display with 4x20 characters. Comes in many colors with LCM2004 IIC attached.
